# Fritzing sketch ttc (saved by Fritzing 0.9.3b)
breadboards: 1

parts:
  S1 = Round Pushbutton
  S2 = Round Pushbutton
  7SEG2 = 7-Segment LED I2C Backpack (yellow)
  Part1 = Arduino Nano (Rev3.0)
  7SEG3 = 7-Segment LED I2C Backpack (yellow)
  J1 = Piezo Speaker

nets:
  GND: S1.leg0, S2.leg0, 7SEG2.GND, Part1.GND, 7SEG3.GND, J1.pin1
  N1: S1.leg1, Part1.D4
  N2: S2.leg1, Part1.D3
  N3: 7SEG2.V+, Part1.5V, 7SEG3.V+
  N4: 7SEG2.SDA, Part1.D11/MOSI
  N5: 7SEG2.SCL, Part1.D12/MISO
  N6: Part1.D2, J1.pin2
  N7: Part1.D9, 7SEG3.SDA
  N8: Part1.D10, 7SEG3.SCL

notes:
  TM1637 display 1
  TM1637 display 2
  Foot pedal 2
  Foot pedal 1
  Buzzer
  +5V
  CLK
  GND
  DIO

custom parts:
  7-Segment LED I2C Backpack (yellow): 4-digit, 7-segment LED Display with I2C Control
